# Fritzing sketch lab-diagrama (saved by Fritzing 1.0.4)
breadboards: 1

parts:
  KY-1 = Keyes Relay [package=THT]
  LED1 = DUO LED RG [package="5 mm [THT]"]
  R1 = Resistor [tolerance=±5% resistance=220 package="2512 [SMD]"]
  R2 = Resistor [tolerance=±5% resistance=220 package="2512 [SMD]"]
  Componente1 = Thumb Joystick
  S1 = Tilt Switch [package=THT]
  R3 = Resistor [tolerance=±5% resistance=10k package="0805 [SMD]"]
  J1 = Basic Servo
  Mod2 = Raspberry Pi Pico W

nets:
  N1: KY-1.signal, Mod2.pin_16
  N2: KY-1.power, Componente1.VCC, S1.Pin_2
  GND: KY-1.ground, LED1.common_cathode, Componente1.GND, R3.Pin_0, J1.gnd, Mod2.pin_34
  N3: LED1.red_anode, R1.Pin_1
  N4: LED1.green_anode, R2.Pin_1
  N5: R1.Pin_0, Mod2.pin_17
  N6: R2.Pin_0, Mod2.pin_3, Mod2.pin_8, Mod2.pin_13, Mod2.pin_18, Mod2.pin_23, Mod2.pin_28, Mod2.pin_33, Mod2.pin_38
  N7: Componente1.VERT, Mod2.pin_31
  N8: S1.Pin_1, R3.Pin_1, Mod2.pin_20
  N9: J1.vcc, Mod2.pin_39
  N10: J1.pulse, Mod2.pin_15

custom parts:
  Keyes Relay: The Keyes 5V relay module is suitable for SCM development, home appliance control. It uses a 5V~12V TIL control signal which can control DC / AC signal.
  Raspberry Pi Pico W: Raspberry Pi Pico W. Based around the RP2040 microcontroller the Pico W is a low cost microcontroller device bringing Raspberry Pi quality, cost, and easy of use to the microcontroller space. The areas marked KEEPOUT in pcb silkscreen should not have traces running through them to avoid shorts on a soldered in module!
